# Fritzing sketch schematic (saved by Fritzing 0.8.7b)
breadboards: 1

parts:
  Pumpcontroller = WeMos D1 Mini
  Seeed_Studio_SPDT_Relais_Modul = KY-019 5V Relay Module [package="Breakout board"]
  Maker_Factory_Analoger_Boden-Feuchtigkeitssensor = FC-28 Soil Hygrometer Module - Probe
  Plantcontroller = WeMos D1 Mini
  Maker_Factory_Analoger_Wasserpegelsensor = Water Level Sensor
  VCC1 = Battery  # not connected
  12V_Peristaltische_Pumpe = DC Motor

nets:
  5V: Pumpcontroller.5V, Seeed_Studio_SPDT_Relais_Modul.+, Maker_Factory_Analoger_Wasserpegelsensor.VCC
  N1: Pumpcontroller.A0, Maker_Factory_Analoger_Wasserpegelsensor.SIG
  N2: Pumpcontroller.D8, Seeed_Studio_SPDT_Relais_Modul.S
  GND: Pumpcontroller.G, Seeed_Studio_SPDT_Relais_Modul.-, Maker_Factory_Analoger_Wasserpegelsensor.GND, 12V_Peristaltische_Pumpe.pin_2
  12V: Seeed_Studio_SPDT_Relais_Modul.Common
  N3: Seeed_Studio_SPDT_Relais_Modul.NO, 12V_Peristaltische_Pumpe.pin_1
  N4: Maker_Factory_Analoger_Boden-Feuchtigkeitssensor.POS, Plantcontroller.5V
  N5: Maker_Factory_Analoger_Boden-Feuchtigkeitssensor.NEG, Plantcontroller.G

custom parts:
  WeMos D1 Mini: The D1 mini is a mini wifi board based on ESP-8266EX.
  KY-019 5V Relay Module: KY-019 5V Relay module, used to control AC circuits.
  FC-28 Soil Hygrometer Module - Probe: The FC-28 is a soil hygrometer module that uses the Texas Instruments LM393 comparator chip to provide an analog measurement of soil humidity.
  Water Level Sensor: A water level sensor. This sensor operates at 3V to 5V. The Sig (signal) pin outputs an analogue signal that is in proportion to the amount of water in contact with the sensor.
